// Logisim project computer.circ as structural Verilog: 25 circuits, main circuit CPU
module semiadder (
  input  A,
  input  B,
  output U,
  output S
);

  and and_1 (U, A, B);
  xor xor_1 (S, A, B);
endmodule

module fulladder (
  input  A,
  input  B,
  input  D,
  output U,
  output S
);

  wire semiadder_1_s, semiadder_1_u, semiadder_2_u;

  semiadder semiadder_1 (.A(A), .B(B), .U(semiadder_1_u), .S(semiadder_1_s));
  semiadder semiadder_2 (.A(semiadder_1_s), .B(D), .U(semiadder_2_u), .S(S));
  or or_1 (U, semiadder_1_u, semiadder_2_u);
endmodule

module Add_8 (
  input  A0,
  input  A1,
  input  A2,
  input  A3,
  input  A4,
  input  A5,
  input  A6,
  input  AN,
  input  B0,
  input  B1,
  input  B2,
  input  B3,
  input  B4,
  input  B5,
  input  B6,
  input  BN,
  output S0,
  output S1,
  output S2,
  output S3,
  output S4,
  output S5,
  output S6,
  output SN,
  output SO
);

  wire fulladder_1_u, fulladder_2_u, fulladder_3_u, fulladder_4_u, fulladder_5_u, fulladder_6_u,
       semiadder_1_u;

  semiadder semiadder_1 (.A(A0), .B(B0), .U(semiadder_1_u), .S(S0));
  fulladder fulladder_1 (.A(A1), .B(B1), .D(semiadder_1_u), .U(fulladder_1_u), .S(S1));
  fulladder fulladder_2 (.A(A2), .B(B2), .D(fulladder_1_u), .U(fulladder_2_u), .S(S2));
  fulladder fulladder_3 (.A(A3), .B(B3), .D(fulladder_2_u), .U(fulladder_3_u), .S(S3));
  fulladder fulladder_4 (.A(A4), .B(B4), .D(fulladder_3_u), .U(fulladder_4_u), .S(S4));
  fulladder fulladder_5 (.A(A5), .B(B5), .D(fulladder_4_u), .U(fulladder_5_u), .S(S5));
  fulladder fulladder_6 (.A(A6), .B(B6), .D(fulladder_5_u), .U(fulladder_6_u), .S(S6));
  fulladder fulladder_7 (.A(AN), .B(BN), .D(fulladder_6_u), .U(SO), .S(SN));
endmodule

module Sel_2 (
  input  L_0_5295f36e,
  input  L_1_e4c21882,
  input  S,
  output U
);

  wire and_1_out, and_2_out, not_1_out;

  and and_1 (and_1_out, L_0_5295f36e, not_1_out);
  not not_1 (not_1_out, S);
  and and_2 (and_2_out, L_1_e4c21882, S);
  or or_1 (U, and_1_out, and_2_out);
endmodule

module Sel_8 (
  input  A0,
  input  A1,
  input  A2,
  input  A3,
  input  A4,
  input  A5,
  input  A6,
  input  AN,
  input  B0,
  input  B1,
  input  B2,
  input  B3,
  input  B4,
  input  B5,
  input  S,
  input  B6,
  input  BN,
  output S0,
  output S1,
  output S2,
  output S3,
  output S4,
  output S5,
  output S6,
  output SN
);

  Sel_2 sel_2_1 (.L_0_5295f36e(A0), .L_1_e4c21882(B0), .S(S), .U(S0));
  Sel_2 sel_2_2 (.L_0_5295f36e(A1), .L_1_e4c21882(B1), .S(S), .U(S1));
  Sel_2 sel_2_3 (.L_0_5295f36e(A2), .L_1_e4c21882(B2), .S(S), .U(S2));
  Sel_2 sel_2_4 (.L_0_5295f36e(A3), .L_1_e4c21882(B3), .S(S), .U(S3));
  Sel_2 sel_2_5 (.L_0_5295f36e(A4), .L_1_e4c21882(B4), .S(S), .U(S4));
  Sel_2 sel_2_6 (.L_0_5295f36e(A5), .L_1_e4c21882(B5), .S(S), .U(S5));
  Sel_2 sel_2_7 (.L_0_5295f36e(A6), .L_1_e4c21882(B6), .S(S), .U(S6));
  Sel_2 sel_2_8 (.L_0_5295f36e(AN), .L_1_e4c21882(BN), .S(S), .U(SN));
endmodule

module Sel_8_M (
  input  [7:0] A,
  input  [7:0] B,
  input  SEL,
  output [7:0] S
);

  Sel_2 sel_2_1 (.L_0_5295f36e(A[0]), .L_1_e4c21882(B[0]), .S(SEL), .U(S[0]));
  Sel_2 sel_2_2 (.L_0_5295f36e(A[1]), .L_1_e4c21882(B[1]), .S(SEL), .U(S[1]));
  Sel_2 sel_2_3 (.L_0_5295f36e(A[2]), .L_1_e4c21882(B[2]), .S(SEL), .U(S[2]));
  Sel_2 sel_2_4 (.L_0_5295f36e(A[3]), .L_1_e4c21882(B[3]), .S(SEL), .U(S[3]));
  Sel_2 sel_2_5 (.L_0_5295f36e(A[4]), .L_1_e4c21882(B[4]), .S(SEL), .U(S[4]));
  Sel_2 sel_2_6 (.L_0_5295f36e(A[5]), .L_1_e4c21882(B[5]), .S(SEL), .U(S[5]));
  Sel_2 sel_2_7 (.L_0_5295f36e(A[6]), .L_1_e4c21882(B[6]), .S(SEL), .U(S[6]));
  Sel_2 sel_2_8 (.L_0_5295f36e(A[7]), .L_1_e4c21882(B[7]), .S(SEL), .U(S[7]));
endmodule

module SW_8 (
  input  A0,
  input  A1,
  input  A2,
  input  A3,
  input  A4,
  input  A5,
  input  A6,
  input  AN,
  input  S,
  output S0,
  output S1,
  output S2,
  output S3,
  output S4,
  output S5,
  output S6,
  output SN
);

  and and_1 (S0, A0, S);
  and and_2 (S1, A1, S);
  and and_3 (S2, A2, S);
  and and_4 (S3, A3, S);
  and and_5 (S4, A4, S);
  and and_6 (S5, A5, S);
  and and_7 (S6, A6, S);
  and and_8 (SN, AN, S);
endmodule

module SW_8_M (
  input  [7:0] A,
  input  E,
  output [7:0] S
);

  SW_8 sw_8_1 (
    .A0(A[0]), .A1(A[1]), .A2(A[2]), .A3(A[3]), .A4(A[4]), .A5(A[5]), .A6(A[6]), .AN(A[7]), .S(E), .S0(S[0]),
    .S1(S[1]), .S2(S[2]), .S3(S[3]), .S4(S[4]), .S5(S[5]), .S6(S[6]), .SN(S[7]));
endmodule

module CMD_2 (
  input  C0,
  input  C1,
  input  E,
  output TT,
  output TF,
  output FT,
  output FF
);

  wire not_1_out, not_2_out;

  not not_1 (not_1_out, C0);
  not not_2 (not_2_out, C1);
  and and_1 (TT, C0, C1, E);
  and and_2 (TF, C0, not_2_out, E);
  and and_3 (FT, not_1_out, C1, E);
  and and_4 (FF, not_1_out, not_2_out, E);
endmodule

module CMD_4 (
  input  [3:0] C,
  output [15:0] O
);

  wire cmd_2_1_ff, cmd_2_1_ft, cmd_2_1_tf, cmd_2_1_tt, cmd_2_2_ff, cmd_2_2_ft, cmd_2_2_tf, cmd_2_2_tt;

  CMD_2 cmd_2_1 (.C0(C[0]), .C1(C[1]), .TT(cmd_2_1_tt), .TF(cmd_2_1_tf), .FT(cmd_2_1_ft), .FF(cmd_2_1_ff));  // open: E
  CMD_2 cmd_2_2 (.C0(C[2]), .C1(C[3]), .TT(cmd_2_2_tt), .TF(cmd_2_2_tf), .FT(cmd_2_2_ft), .FF(cmd_2_2_ff));  // open: E
  // AND_Gate and_1 has open pins: in0=cmd_2_2_tt, in1=cmd_2_1_tt, out=open
  // AND_Gate and_2 has open pins: in0=cmd_2_2_tf, in1=cmd_2_1_tt, out=open
  // AND_Gate and_3 has open pins: in0=cmd_2_2_ft, in1=cmd_2_1_tt, out=open
  // AND_Gate and_4 has open pins: in0=cmd_2_2_ff, in1=cmd_2_1_tt, out=open
  // AND_Gate and_5 has open pins: in0=cmd_2_2_tt, in1=cmd_2_1_tf, out=open
  // AND_Gate and_6 has open pins: in0=cmd_2_2_tf, in1=cmd_2_1_tf, out=open
  // AND_Gate and_7 has open pins: in0=cmd_2_2_ft, in1=cmd_2_1_tf, out=open
  // AND_Gate and_8 has open pins: in0=cmd_2_2_ff, in1=cmd_2_1_tf, out=open
  // AND_Gate and_9 has open pins: in0=cmd_2_2_tt, in1=cmd_2_1_ft, out=open
  // AND_Gate and_10 has open pins: in0=cmd_2_2_tf, in1=cmd_2_1_ft, out=open
  // AND_Gate and_11 has open pins: in0=cmd_2_2_ft, in1=cmd_2_1_ft, out=open
  // AND_Gate and_12 has open pins: in0=cmd_2_2_ff, in1=cmd_2_1_ft, out=open
  // AND_Gate and_13 has open pins: in0=cmd_2_2_tt, in1=cmd_2_1_ff, out=open
  // AND_Gate and_14 has open pins: in0=cmd_2_2_tf, in1=cmd_2_1_ff, out=open
  // AND_Gate and_15 has open pins: in0=cmd_2_2_ft, in1=cmd_2_1_ff, out=open
  // AND_Gate and_16 has open pins: in0=cmd_2_2_ff, in1=cmd_2_1_ff, out=open
endmodule

module Div_2 (
  input  S,
  input  L_0_5295f36e,
  output U0,
  output U1
);

  wire not_1_out;

  not not_1 (not_1_out, S);
  and and_1 (U0, not_1_out, L_0_5295f36e);
  and and_2 (U1, L_0_5295f36e, S);
endmodule

module Div_8_M (
  input  [7:0] D,
  input  in_2,
  output [7:0] A,
  output [7:0] B
);

  Div_2 div_2_1 (.L_0_5295f36e(D[0]), .S(in_2), .U0(A[0]), .U1(B[0]));
  Div_2 div_2_2 (.L_0_5295f36e(D[1]), .S(in_2), .U0(A[1]), .U1(B[1]));
  Div_2 div_2_3 (.L_0_5295f36e(D[2]), .S(in_2), .U0(A[2]), .U1(B[2]));
  Div_2 div_2_4 (.L_0_5295f36e(D[3]), .S(in_2), .U0(A[3]), .U1(B[3]));
  Div_2 div_2_5 (.L_0_5295f36e(D[4]), .S(in_2), .U0(A[4]), .U1(B[4]));
  Div_2 div_2_6 (.L_0_5295f36e(D[5]), .S(in_2), .U0(A[5]), .U1(B[5]));
  Div_2 div_2_7 (.L_0_5295f36e(D[6]), .S(in_2), .U0(A[6]), .U1(B[6]));
  Div_2 div_2_8 (.L_0_5295f36e(D[7]), .S(in_2), .U0(A[7]), .U1(B[7]));
endmodule

module D_Ratch (
  input  S,
  input  D,
  input  CLK,
  input  E,
  input  R,
  output U,
  output NOT_U_ac6da121
);

  wire and_1_out, and_2_out, and_3_out, and_4_out, nor_1_out, nor_2_out, nor_3_out;

  and and_1 (and_1_out, D, CLK);
  and and_2 (and_2_out, CLK, E);
  nor nor_1 (nor_1_out, S, R);
  and and_3 (and_3_out, and_1_out, and_2_out, nor_1_out);
  and and_4 (and_4_out, nor_1_out, ~and_1_out, and_2_out);  // AND_Gate
  nor nor_2 (nor_2_out, S, and_3_out);
  nor nor_3 (nor_3_out, and_4_out, R);
  nand nand_1 (U, nor_2_out, NOT_U_ac6da121);
  nand nand_2 (NOT_U_ac6da121, U, nor_3_out);
endmodule

module D_8 (
  input  [7:0] D,
  input  CLK,
  input  E,
  input  R,
  output [7:0] U
);

  D_Ratch d_ratch_1 (.D(D[0]), .CLK(CLK), .E(E), .S(1'b0), .R(R), .U(U[0]));  // open: NOT_U_ac6da121
  D_Ratch d_ratch_2 (.D(D[1]), .CLK(CLK), .E(E), .S(1'b0), .R(R), .U(U[1]));  // open: NOT_U_ac6da121
  D_Ratch d_ratch_3 (.D(D[2]), .CLK(CLK), .E(E), .S(1'b0), .R(R), .U(U[2]));  // open: NOT_U_ac6da121
  D_Ratch d_ratch_4 (.D(D[3]), .CLK(CLK), .E(E), .S(1'b0), .R(R), .U(U[3]));  // open: NOT_U_ac6da121
  D_Ratch d_ratch_5 (.D(D[4]), .CLK(CLK), .E(E), .S(1'b0), .R(R), .U(U[4]));  // open: NOT_U_ac6da121
  D_Ratch d_ratch_6 (.D(D[5]), .CLK(CLK), .E(E), .S(1'b0), .R(R), .U(U[5]));  // open: NOT_U_ac6da121
  D_Ratch d_ratch_7 (.D(D[6]), .CLK(CLK), .E(E), .S(1'b0), .R(R), .U(U[6]));  // open: NOT_U_ac6da121
  D_Ratch d_ratch_8 (.D(D[7]), .CLK(CLK), .E(E), .S(1'b0), .R(R), .U(U[7]));  // open: NOT_U_ac6da121
endmodule

module M_S_D_Flip_Flop (
  input  D,
  input  CLK,
  input  E,
  input  R,
  output U,
  output Not_U
);

  wire d_ratch_1_u, not_1_out;

  D_Ratch d_ratch_1 (.D(D), .CLK(CLK), .E(E), .S(1'b0), .R(R), .U(d_ratch_1_u));  // open: NOT_U_ac6da121
  not not_1 (not_1_out, CLK);
  D_Ratch d_ratch_2 (.D(d_ratch_1_u), .CLK(not_1_out), .E(E), .S(1'b0), .R(R), .U(U), .NOT_U_ac6da121(Not_U));
endmodule

module M_S_D_8 (
  input  [7:0] D,
  input  CLK,
  input  E,
  input  R,
  output [7:0] U
);

  wire not_1_out;
  wire [7:0] d_8_1_u;

  D_8 d_8_1 (.D(D), .CLK(CLK), .E(E), .R(R), .U(d_8_1_u));
  not not_1 (not_1_out, CLK);
  D_8 d_8_2 (.D(d_8_1_u), .CLK(not_1_out), .E(E), .R(R), .U(U));
endmodule

module Merger_8 (
  input  A0,
  input  A1,
  input  A2,
  input  A3,
  input  A4,
  input  A5,
  input  A6,
  input  AN,
  input  B0,
  input  B1,
  input  B2,
  input  B3,
  input  B4,
  input  B5,
  input  B6,
  input  BN,
  output S0,
  output S1,
  output S2,
  output S3,
  output S4,
  output S5,
  output S6,
  output SN
);

  or or_1 (S0, A0, B0);
  or or_2 (S1, A1, B1);
  or or_3 (S2, A2, B2);
  or or_4 (S3, A3, B3);
  or or_5 (S4, A4, B4);
  or or_6 (S5, A5, B5);
  or or_7 (S6, A6, B6);
  or or_8 (SN, AN, BN);
endmodule

module Counter_2 (
  input  E,
  input  CLK,
  input  C,
  output L_0,
  output L_1
);

  J_K_Flip_Flop #(.trigger("falling")) j_k_ff_1 (.J(E), .K(E), .clk(CLK), .Q(L_0), .reset(C));  // open: Qn, preset
  J_K_Flip_Flop #(.trigger("falling")) j_k_ff_2 (.J(E), .K(E), .clk(L_0), .Q(L_1), .reset(C));  // open: Qn, preset
endmodule

module Counter_8 (
  input  E,
  input  CLK,
  input  C,
  output L_0,
  output L_1,
  output L_2,
  output L_3,
  output L_4,
  output L_5,
  output L_6,
  output L_7
);

  J_K_Flip_Flop j_k_ff_1 (.J(E), .K(E), .clk(CLK), .Q(L_0), .reset(C));  // open: Qn, preset
  J_K_Flip_Flop #(.trigger("falling")) j_k_ff_2 (.J(E), .K(E), .clk(L_0), .Q(L_1), .reset(C));  // open: Qn, preset
  J_K_Flip_Flop #(.trigger("falling")) j_k_ff_3 (.J(E), .K(E), .clk(L_1), .Q(L_2), .reset(C));  // open: Qn, preset
  J_K_Flip_Flop #(.trigger("falling")) j_k_ff_4 (.J(E), .K(E), .clk(L_2), .Q(L_3), .reset(C));  // open: Qn, preset
  J_K_Flip_Flop #(.trigger("falling")) j_k_ff_5 (.J(E), .K(E), .clk(L_3), .Q(L_4), .reset(C));  // open: Qn, preset
  J_K_Flip_Flop #(.trigger("falling")) j_k_ff_6 (.J(E), .K(E), .clk(L_4), .Q(L_5), .reset(C));  // open: Qn, preset
  J_K_Flip_Flop #(.trigger("falling")) j_k_ff_7 (.J(E), .K(E), .clk(L_5), .Q(L_6), .reset(C));  // open: Qn, preset
  J_K_Flip_Flop #(.trigger("falling")) j_k_ff_8 (.J(E), .K(E), .clk(L_6), .Q(L_7), .reset(C));  // open: Qn, preset
endmodule

module Inverter (
  input  A0,
  input  A1,
  input  A2,
  input  A3,
  input  A4,
  input  A5,
  input  A6,
  input  AN,
  output S0,
  output S1,
  output S2,
  output S3,
  output S4,
  output S5,
  output S6,
  output SN
);

  wire not_1_out, not_2_out, not_3_out, not_4_out, not_5_out, not_6_out, not_7_out, not_8_out;

  not not_1 (not_1_out, A0);
  not not_2 (not_2_out, A1);
  not not_3 (not_3_out, A2);
  not not_4 (not_4_out, A3);
  not not_5 (not_5_out, A4);
  not not_6 (not_6_out, A5);
  not not_7 (not_7_out, A6);
  not not_8 (not_8_out, AN);
  Add_8 add_8_1 (
    .A0(not_1_out), .A1(not_2_out), .A2(not_3_out), .A3(not_4_out), .A4(not_5_out), .A5(not_6_out),
    .A6(not_7_out), .AN(not_8_out), .B0(1'b1), .B1(1'b0), .B2(1'b0), .B3(1'b0), .B4(1'b0), .B5(1'b0),
    .B6(1'b0), .BN(1'b0), .S0(S0), .S1(S1), .S2(S2), .S3(S3), .S4(S4), .S5(S5), .S6(S6), .SN(SN));  // open: SO
endmodule

module AddSub (
  input  A0,
  input  A1,
  input  A2,
  input  A3,
  input  A4,
  input  A5,
  input  A6,
  input  AN,
  input  RUN,
  input  CLK,
  input  SUB,
  input  B0,
  input  B1,
  input  B2,
  input  B3,
  input  B4,
  input  B5,
  input  B6,
  input  BN,
  output S0,
  output S1,
  output S2,
  output S3,
  output S4,
  output S5,
  output S6,
  output SN
);

  wire and_1_out, and_2_out, inverter_1_s0, inverter_1_s1, inverter_1_s2, inverter_1_s3, inverter_1_s4,
       inverter_1_s5, inverter_1_s6, inverter_1_sn, sel_8_1_s0, sel_8_1_s1, sel_8_1_s2, sel_8_1_s3,
       sel_8_1_s4, sel_8_1_s5, sel_8_1_s6, sel_8_1_sn, sw_8_1_s0, sw_8_1_s1, sw_8_1_s2, sw_8_1_s3, sw_8_1_s4,
       sw_8_1_s5, sw_8_1_s6, sw_8_1_sn, sw_8_2_s0, sw_8_2_s1, sw_8_2_s2, sw_8_2_s3, sw_8_2_s4, sw_8_2_s5,
       sw_8_2_s6, sw_8_2_sn;

  and and_1 (and_1_out, RUN, CLK);
  and and_2 (and_2_out, and_1_out, SUB);
  SW_8 sw_8_1 (
    .A0(B0), .A1(B1), .A2(B2), .A3(B3), .A4(B4), .A5(B5), .A6(B6), .AN(BN), .S(and_1_out), .S0(sw_8_1_s0),
    .S1(sw_8_1_s1), .S2(sw_8_1_s2), .S3(sw_8_1_s3), .S4(sw_8_1_s4), .S5(sw_8_1_s5), .S6(sw_8_1_s6),
    .SN(sw_8_1_sn));
  SW_8 sw_8_2 (
    .A0(AN), .A1(A6), .A2(A5), .A3(A4), .A4(A3), .A5(A2), .A6(A1), .AN(A0), .S(and_1_out), .S0(sw_8_2_s0),
    .S1(sw_8_2_s1), .S2(sw_8_2_s2), .S3(sw_8_2_s3), .S4(sw_8_2_s4), .S5(sw_8_2_s5), .S6(sw_8_2_s6),
    .SN(sw_8_2_sn));
  Inverter inverter_1 (
    .A0(sw_8_1_s0), .A1(sw_8_1_s1), .A2(sw_8_1_s2), .A3(sw_8_1_s3), .A4(sw_8_1_s4), .A5(sw_8_1_s5),
    .A6(sw_8_1_s6), .AN(sw_8_1_sn), .S0(inverter_1_s0), .S1(inverter_1_s1), .S2(inverter_1_s2),
    .S3(inverter_1_s3), .S4(inverter_1_s4), .S5(inverter_1_s5), .S6(inverter_1_s6), .SN(inverter_1_sn));
  Sel_8 sel_8_1 (
    .A0(sw_8_1_s0), .A1(sw_8_1_s1), .A2(sw_8_1_s2), .A3(sw_8_1_s3), .A4(sw_8_1_s4), .A5(sw_8_1_s5),
    .A6(sw_8_1_s6), .AN(sw_8_1_sn), .B0(inverter_1_s0), .B1(inverter_1_s1), .B2(inverter_1_s2),
    .B3(inverter_1_s3), .B4(inverter_1_s4), .B5(inverter_1_s5), .B6(inverter_1_s6), .BN(inverter_1_sn),
    .S(and_2_out), .S0(sel_8_1_s0), .S1(sel_8_1_s1), .S2(sel_8_1_s2), .S3(sel_8_1_s3), .S4(sel_8_1_s4),
    .S5(sel_8_1_s5), .S6(sel_8_1_s6), .SN(sel_8_1_sn));
  Add_8 add_8_1 (
    .A0(sw_8_2_sn), .A1(sw_8_2_s6), .A2(sw_8_2_s5), .A3(sw_8_2_s4), .A4(sw_8_2_s3), .A5(sw_8_2_s2),
    .A6(sw_8_2_s1), .AN(sw_8_2_s0), .B0(sel_8_1_s0), .B1(sel_8_1_s1), .B2(sel_8_1_s2), .B3(sel_8_1_s3),
    .B4(sel_8_1_s4), .B5(sel_8_1_s5), .B6(sel_8_1_s6), .BN(sel_8_1_sn), .S0(S0), .S1(S1), .S2(S2), .S3(S3),
    .S4(S4), .S5(S5), .S6(S6), .SN(SN));  // open: SO
endmodule

module Buffer (
  input  [7:0] C,
  input  [7:0] D1,
  input  [7:0] D2,
  input  R,
  input  CLK,
  input  W,
  output [3:0] P,
  output [3:0] U,
  output [7:0] U1,
  output [7:0] U2
);

  wire not_1_out;
  wire [7:0] C2_u, C3_u, C4_u, C5_u, CT2_u, CT3_u, CT4_u, CT5_u, D1CT4_u, D1T2_u, D1T3_u, D1T5_u, D2T2_u,
       D2T3_u, D2T4_u, D2T5_u, D12_u, D13_u, D14_u, D15_u, D22_u, D23_u, D24_u, D25_u;

  D_8 C5 (.D(C), .CLK(CLK), .E(W), .R(R), .U(C5_u));
  D_8 CT5 (.D(C5_u), .CLK(not_1_out), .E(W), .R(R), .U(CT5_u));
  D_8 D15 (.D(D1), .CLK(CLK), .E(W), .R(R), .U(D15_u));
  D_8 D1T5 (.D(D15_u), .CLK(not_1_out), .E(W), .R(R), .U(D1T5_u));
  D_8 D25 (.D(D2), .CLK(CLK), .E(W), .R(R), .U(D25_u));
  D_8 D2T5 (.D(D25_u), .CLK(not_1_out), .E(W), .R(R), .U(D2T5_u));
  not not_1 (not_1_out, CLK);
  D_8 C4 (.D(CT5_u), .CLK(CLK), .E(W), .R(R), .U(C4_u));
  D_8 CT4 (.D(C4_u), .CLK(not_1_out), .E(W), .R(R), .U(CT4_u));
  D_8 D14 (.D(D1T5_u), .CLK(CLK), .E(W), .R(R), .U(D14_u));
  D_8 D1CT4 (.D(D14_u), .CLK(not_1_out), .E(W), .R(R), .U(D1CT4_u));
  D_8 D24 (.D(D2T5_u), .CLK(CLK), .E(W), .R(R), .U(D24_u));
  D_8 D2T4 (.D(D24_u), .CLK(not_1_out), .E(W), .R(R), .U(D2T4_u));
  D_8 C3 (.D(CT4_u), .CLK(CLK), .E(W), .R(R), .U(C3_u));
  D_8 D13 (.D(D1CT4_u), .CLK(CLK), .E(W), .R(R), .U(D13_u));
  D_8 D23 (.D(D2T4_u), .CLK(CLK), .E(W), .R(R), .U(D23_u));
  D_8 CT3 (.D(C3_u), .CLK(not_1_out), .E(W), .R(R), .U(CT3_u));
  D_8 C2 (.D(CT3_u), .CLK(CLK), .E(W), .R(R), .U(C2_u));
  D_8 D1T3 (.D(D13_u), .CLK(not_1_out), .E(W), .R(R), .U(D1T3_u));
  D_8 D12 (.D(D1T3_u), .CLK(CLK), .E(W), .R(R), .U(D12_u));
  D_8 D2T3 (.D(D23_u), .CLK(not_1_out), .E(W), .R(R), .U(D2T3_u));
  D_8 D22 (.D(D2T3_u), .CLK(CLK), .E(W), .R(R), .U(D22_u));
  D_8 CT2 (.D(C2_u), .CLK(not_1_out), .E(W), .R(R), .U(CT2_u));
  D_8 D1T2 (.D(D12_u), .CLK(not_1_out), .E(W), .R(R), .U(D1T2_u));
  D_8 D2T2 (.D(D22_u), .CLK(not_1_out), .E(W), .R(R), .U(D2T2_u));
  D_8 C1 (.D(CT2_u), .CLK(CLK), .E(W), .R(R), .U({P, U}));
  D_8 D11 (.D(D1T2_u), .CLK(CLK), .E(W), .R(R), .U(U1));
  D_8 D21 (.D(D2T2_u), .CLK(CLK), .E(W), .R(R), .U(U2));
endmodule

module PU (
  input  [7:0] D1,
  input  R,
  input  CLK,
  input  E,
  input  [3:0] C,
  input  [7:0] D2,
  output [7:0] O
);

  wire and_1_out, and_2_out, and_3_out, and_4_out, and_5_out, clock_1_out, D_Flip_Flop_Reset_u, nor_1_out,
       nor_2_out, not_1_out, or_1_out, or_2_out, Sel_2_Counter_u;
  wire [7:0] ADD_SUB_s0, Counter_8_muldiv_l_0, D_Flip_Flop_8_d1_u, D_Flip_Flop_8_d2_u, D_Flip_Flop_8_r_u,
       Sel_8_D1_s, Sel_8_d1S_s, Sel_8_D2_s, Sel_8_Mul_s, Sel_8_rd1_s, SW_8_Write_s, xor_1_out;

  Clock clock_1 (.out(clock_1_out));
  and and_1 (and_1_out, clock_1_out, E);
  Sel_8_M Sel_8_d1S (.A(ADD_SUB_s0), .B(D1), .SEL(and_2_out), .S(Sel_8_d1S_s));
  M_S_D_8 D_Flip_Flop_8_r (.CLK(and_1_out), .E(C[1]), .R(or_1_out), .D(Sel_8_d1S_s), .U(D_Flip_Flop_8_r_u));
  Sel_8_M Sel_8_D1 (.A(D1), .B(D_Flip_Flop_8_r_u), .SEL(C[1]), .S(Sel_8_D1_s));
  Sel_8_M Sel_8_D2 (.A(D2), .B(Sel_8_rd1_s), .SEL(C[1]), .S(Sel_8_D2_s));
  Sel_8_M Sel_8_rd1 (.A(D_Flip_Flop_8_d1_u), .B(D_Flip_Flop_8_d2_u), .SEL(C[0]), .S(Sel_8_rd1_s));
  M_S_D_8 D_Flip_Flop_8_d2 (.CLK(and_1_out), .E(and_2_out), .R(or_1_out), .D(D2), .U(D_Flip_Flop_8_d2_u));
  AddSub ADD_SUB (
    .RUN(E), .CLK(clock_1_out), .SUB(C[0]), .A0(Sel_8_D1_s[0]), .A1(Sel_8_D1_s[1]), .A2(Sel_8_D1_s[2]),
    .A3(Sel_8_D1_s[3]), .A4(Sel_8_D1_s[4]), .A5(Sel_8_D1_s[5]), .A6(Sel_8_D1_s[6]), .AN(Sel_8_D1_s[7]),
    .B0(Sel_8_D2_s[0]), .B1(Sel_8_D2_s[1]), .B2(Sel_8_D2_s[2]), .B3(Sel_8_D2_s[3]), .B4(Sel_8_D2_s[4]),
    .B5(Sel_8_D2_s[5]), .B6(Sel_8_D2_s[6]), .BN(Sel_8_D2_s[7]), .S0(ADD_SUB_s0[0]), .S1(ADD_SUB_s0[1]),
    .S2(ADD_SUB_s0[2]), .S3(ADD_SUB_s0[3]), .S4(ADD_SUB_s0[4]), .S5(ADD_SUB_s0[5]), .S6(ADD_SUB_s0[6]),
    .SN(ADD_SUB_s0[7]));
  M_S_D_8 D_Flip_Flop_8_d1 (.CLK(and_1_out), .E(C[1]), .R(or_1_out), .D(D1), .U(D_Flip_Flop_8_d1_u));
  or or_1 (or_1_out, D_Flip_Flop_Reset_u, R);
  assign xor_1_out = D_Flip_Flop_8_d2_u ^ Counter_8_muldiv_l_0;  // XOR_Gate xor_1, 8 bits wide
  M_S_D_Flip_Flop D_Flip_Flop_Reset (
    .D(or_2_out), .CLK(and_1_out), .E(1'b1), .R(R), .U(D_Flip_Flop_Reset_u));  // open: Not_U
  nor nor_1 (nor_1_out, xor_1_out[0], xor_1_out[1], xor_1_out[2], xor_1_out[3], xor_1_out[4], xor_1_out[5], xor_1_out[6], xor_1_out[7]);
  Sel_2 Sel_2_Counter (.L_0_5295f36e(nor_1_out), .L_1_e4c21882(ADD_SUB_s0[7]), .S(C[0]), .U(Sel_2_Counter_u));
  and and_2 (and_2_out, C[1], nor_2_out);
  nor nor_2 (nor_2_out, Counter_8_muldiv_l_0[7], Counter_8_muldiv_l_0[6], Counter_8_muldiv_l_0[5], Counter_8_muldiv_l_0[4], Counter_8_muldiv_l_0[3], Counter_8_muldiv_l_0[2], Counter_8_muldiv_l_0[1], Counter_8_muldiv_l_0[0]);
  SW_8_M SW_8_Write (.A(D_Flip_Flop_8_r_u), .E(and_4_out), .S(SW_8_Write_s));
  and and_3 (and_3_out, nor_1_out, Sel_2_Counter_u);
  not not_1 (not_1_out, Sel_2_Counter_u);
  Sel_8_M Sel_8_Mul (.A(ADD_SUB_s0), .B(SW_8_Write_s), .SEL(C[1]), .S(Sel_8_Mul_s));
  and and_4 (and_4_out, C[1], and_3_out);
  Counter_8 Counter_8_muldiv (
    .E(not_1_out), .CLK(and_1_out), .C(or_1_out), .L_0(Counter_8_muldiv_l_0[0]),
    .L_1(Counter_8_muldiv_l_0[1]), .L_2(Counter_8_muldiv_l_0[2]), .L_3(Counter_8_muldiv_l_0[3]),
    .L_4(Counter_8_muldiv_l_0[4]), .L_5(Counter_8_muldiv_l_0[5]), .L_6(Counter_8_muldiv_l_0[6]),
    .L_7(Counter_8_muldiv_l_0[7]));
  or or_2 (or_2_out, O[7], O[6], O[5], O[4], O[3], O[2], O[1], O[0]);
  and and_5 (and_5_out, Sel_2_Counter_u, C[1], C[0]);
  Sel_8_M Sel_8_Write (.A(Sel_8_Mul_s), .B(Counter_8_muldiv_l_0), .SEL(and_5_out), .S(O));

  // Notes on the sheet:
  //   CLK
  //   1
  //   1
  //   CLK
  //   CLK
  //   1
  //   1
  //   0
  //   CLK
endmodule

module Regist (
  input  [7:0] D1,
  input  R,
  input  CLK,
  input  E,
  input  [3:0] C,
  input  [7:0] D2,
  output [7:0] S
);

  wire and_1_out, and_2_out, cmd_2_1_ff, cmd_2_1_ft, cmd_2_1_tf, cmd_2_2_ff, cmd_2_2_ft, cmd_2_2_tf,
       cmd_2_2_tt, counter_2_1_l_0, counter_2_1_l_1, not_1_out, or_1_out, or_2_out, or_3_out;
  wire [7:0] div_8_m_1_a, m_s_d_8_1_u, m_s_d_8_2_u, R0_u, R1_u, R2_u, R3_u, sel_8_m_1_s, sel_8_m_2_s,
       sel_8_m_3_s, sel_8_m_4_s, sel_8_m_5_s, sel_8_m_6_s, sw_8_m_1_s, undriven_2;
  wire [7:4] undriven;

  and and_1 (and_1_out, CLK, E);
  or or_1 (or_1_out, R, cmd_2_1_tf);
  M_S_D_8 m_s_d_8_1 (.CLK(and_1_out), .E(cmd_2_1_ff), .R(or_1_out), .D({undriven, C}), .U(m_s_d_8_1_u));
  M_S_D_8 m_s_d_8_2 (.CLK(and_1_out), .E(C[1]), .R(or_1_out), .D(D1), .U(m_s_d_8_2_u));
  Sel_8_M sel_8_m_1 (.A(D1), .B(m_s_d_8_2_u), .SEL(cmd_2_1_ft), .S(sel_8_m_1_s));
  Sel_8_M sel_8_m_2 (.A(sel_8_m_1_s), .B(D2), .SEL(C[1]), .S(sel_8_m_2_s));
  or or_2 (or_2_out, C[1], counter_2_1_l_0, counter_2_1_l_1);
  or or_3 (or_3_out, m_s_d_8_1_u[1], C[1]);
  Counter_2 counter_2_1 (.E(or_2_out), .CLK(and_1_out), .C(or_1_out), .L_0(counter_2_1_l_0), .L_1(counter_2_1_l_1));
  CMD_2 cmd_2_1 (
    .C0(counter_2_1_l_1), .C1(counter_2_1_l_0), .E(or_3_out), .TF(cmd_2_1_tf), .FT(cmd_2_1_ft),
    .FF(cmd_2_1_ff));  // open: TT
  Sel_8_M sel_8_m_3 (.A(D2), .B(undriven_2), .SEL(or_3_out), .S(sel_8_m_3_s));
  CMD_2 cmd_2_2 (
    .C0(sel_8_m_2_s[0]), .C1(sel_8_m_2_s[1]), .E(not_1_out), .TT(cmd_2_2_tt), .TF(cmd_2_2_tf),
    .FT(cmd_2_2_ft), .FF(cmd_2_2_ff));
  not not_1 (not_1_out, C[0]);
  SW_8_M sw_8_m_1 (.A(undriven_2), .S(sw_8_m_1_s));  // open: E
  // AND_Gate and_2 has open pins: out=and_2_out
  M_S_D_8 R0 (.CLK(and_1_out), .E(cmd_2_2_tt), .R(or_1_out), .D(sel_8_m_3_s), .U(R0_u));
  M_S_D_8 R1 (.CLK(and_1_out), .E(cmd_2_2_tf), .R(or_1_out), .D(sel_8_m_3_s), .U(R1_u));
  M_S_D_8 R2 (.CLK(and_1_out), .E(cmd_2_2_ft), .R(or_1_out), .D(sel_8_m_3_s), .U(R2_u));
  M_S_D_8 R3 (.CLK(and_1_out), .E(cmd_2_2_ff), .R(or_1_out), .D(sel_8_m_3_s), .U(R3_u));
  M_S_D_8 m_s_d_8_3 (.CLK(and_1_out), .E(and_2_out), .R(or_1_out), .D(div_8_m_1_a), .U(sw_8_m_1_s));
  Sel_8_M sel_8_m_4 (.A(R0_u), .B(R1_u), .SEL(sel_8_m_2_s[0]), .S(sel_8_m_4_s));
  Sel_8_M sel_8_m_5 (.A(R2_u), .B(R3_u), .SEL(sel_8_m_2_s[0]), .S(sel_8_m_5_s));
  Sel_8_M sel_8_m_6 (.A(sel_8_m_4_s), .B(sel_8_m_5_s), .SEL(sel_8_m_2_s[1]), .S(sel_8_m_6_s));
  Div_8_M div_8_m_1 (.D(sel_8_m_6_s), .in_2(C[0]), .A(div_8_m_1_a), .B(S));
endmodule

module CPU (
  input  D17,
  input  D16,
  input  D15,
  input  D14,
  input  D13,
  input  D12,
  input  D11,
  input  D10,
  input  C0,
  input  C1,
  input  C2,
  input  C3,
  input  C4,
  input  C5,
  input  C6,
  input  C7,
  input  R,
  input  D27,
  input  D26,
  input  D25,
  input  D24,
  input  D23,
  input  D22,
  input  D21,
  input  D20,
  output U0,
  output U1,
  output U2,
  output U3,
  output U4,
  output U5,
  output U6,
  output U7
);

  wire and_2_out, clock_1_out;
  wire [3:0] buffer_1_p, buffer_1_u;
  wire [7:0] buffer_1_u1, buffer_1_u2;

  Clock clock_1 (.out(clock_1_out));
  Buffer buffer_1 (
    .C({C7, C6, C5, C4, C3, C2, C1, C0}), .D1({D17, D16, D15, D14, D13, D12, D11, D10}),
    .D2({D27, D26, D25, D24, D23, D22, D21, D20}), .R(R), .CLK(clock_1_out), .W(1'b1), .P(buffer_1_p),
    .U(buffer_1_u), .U1(buffer_1_u1), .U2(buffer_1_u2));
  // AND_Gate and_1 has open pins: in0=buffer_1_p[2], in1=buffer_1_p[3], out=open
  and and_2 (and_2_out, ~buffer_1_p[2], buffer_1_p[3]);  // AND_Gate
  PU pu_1 (
    .R(R), .CLK(clock_1_out), .E(and_2_out), .C(buffer_1_u), .D1(buffer_1_u1), .D2(buffer_1_u2),
    .O({U7, U6, U5, U4, U3, U2, U1, U0}));
  LED led_1 (.in(U0));
  LED led_2 (.in(U1));
  LED led_3 (.in(U2));
  LED led_4 (.in(U3));
  LED led_5 (.in(U4));
  LED led_6 (.in(U5));
  LED led_7 (.in(U6));
  LED led_8 (.in(U7));
endmodule
