// Logisim project test.circ as structural Verilog: 4 circuits, main circuit main
module main (
  input  in_1,
  input  in_2,
  input  in_3,
  input  [6:0] in_4,
  input  in_5,
  input  in_6,
  input  in_7,
  input  [3:0] in_8,
  input  in_9,
  input  in_10,
  input  in_11,
  input  in_12,
  input  in_13,
  input  [6:0] in_14,
  input  [6:0] in_15,
  input  [6:0] in_16,
  input  [6:0] in_17,
  input  [6:0] in_18,
  output out_19,
  output out_20,
  output out_21,
  output out_22
);

  wire button_1_out, button_2_out, button_3_out, button_4_out, button_5_out, or_1_out, or_2_out;
  wire [6:0] keyboard_1_data;

  Button button_1 (.out(button_1_out));
  Button button_2 (.out(button_2_out));
  Button button_3 (.out(button_3_out));
  or or_1 (or_1_out, button_1_out, button_2_out);
  or or_2 (or_2_out, button_2_out, button_3_out);
  Keyboard keyboard_1 (.clk(or_2_out), .re(in_13), .clr(button_4_out), .avail(out_19), .data(keyboard_1_data));
  Button button_4 (.out(button_4_out));
  Clock clock_1 (.out(out_20));
  TTY tty_1 (.data(keyboard_1_data), .clk(or_1_out), .we(in_6), .clr(button_5_out));
  Button button_5 (.out(button_5_out));
  DotMatrix dotmatrix_1 (.col0(in_14), .col1(in_15), .col2(in_16), .col3(in_17), .col4(in_18));
  Hex_Digit_Display hex_digit_display_1 (.value(in_8), .dp(in_10));
  _7_Segment_Display u_7_segment_display_1 (
    .g(in_5), .f(in_3), .a(in_2), .b(in_1), .e(in_7), .d(in_9), .c(in_11), .dp(in_12));
  Transistor transistor_1 ();  // open: in, out, gate

  assign out_21 = 1'b0;
  assign out_22 = 1'b1;
endmodule

module counter (
  input  in_1,
  output out_2,
  output out_3,
  output out_4
);

  wire clock_1_out;

  Clock clock_1 (.out(clock_1_out));
  J_K_Flip_Flop #(.trigger("falling")) j_k_ff_1 (
    .J(in_1), .clk(clock_1_out), .K(in_1), .Q(out_2));  // open: Qn, preset, en, reset
  J_K_Flip_Flop #(.trigger("falling")) j_k_ff_2 (
    .J(in_1), .clk(out_2), .K(in_1), .Q(out_3));  // open: Qn, preset, en, reset
  J_K_Flip_Flop #(.trigger("falling")) j_k_ff_3 (
    .J(in_1), .clk(out_3), .K(in_1), .Q(out_4));  // open: Qn, preset, en, reset
endmodule

module shift_register (
  input  in_1
);

  wire clock_1_out, d_ff_2_q, d_ff_3_q;

  Clock clock_1 (.out(clock_1_out));
  D_Flip_Flop d_ff_1 ();  // open: clk, D, Q, Qn, preset, en, reset
  D_Flip_Flop d_ff_2 (.clk(clock_1_out), .D(in_1), .Q(d_ff_2_q));  // open: Qn, preset, en, reset
  D_Flip_Flop d_ff_3 (.clk(clock_1_out), .D(d_ff_2_q), .Q(d_ff_3_q));  // open: Qn, preset, en, reset
  D_Flip_Flop d_ff_4 (.clk(clock_1_out), .D(d_ff_3_q));  // open: Q, Qn, preset, en, reset
endmodule

module _1 (
  input  in_1,
  input  in_2,
  input  in_3,
  input  in_4,
  output out_5,
  output out_6,
  output out_7
);

  wire nor_1_out;

  nor nor_1 (nor_1_out, out_5, in_1);
  nor nor_2 (out_6, in_3, out_7);
  nor nor_3 (out_7, out_6, in_4);
  nor nor_4 (out_5, nor_1_out, in_2);
endmodule
