// Logisim project test.circ as structural Verilog: 1 circuit, main circuit main
module main (
  input  in_1,
  input  in_2,
  input  in_3,
  input  [6:0] in_4,
  input  in_5,
  input  in_6,
  input  in_7,
  input  [3:0] in_8,
  input  in_9,
  input  in_10,
  input  in_11,
  input  in_12,
  input  in_13,
  input  [6:0] in_14,
  input  [6:0] in_15,
  input  [6:0] in_16,
  input  [6:0] in_17,
  input  [6:0] in_18,
  output out_19
);

  wire button_1_out, button_3_out, button_4_out;
  wire [6:0] keyboard_1_data;

  Button button_1 (.out(button_1_out));
  Button button_2 ();  // open: out
  Keyboard keyboard_1 (.clk(button_1_out), .re(in_13), .clr(button_3_out), .avail(out_19), .data(keyboard_1_data));
  Button button_3 (.out(button_3_out));
  TTY tty_1 (.data(keyboard_1_data), .clk(button_1_out), .we(in_6), .clr(button_4_out));
  Button button_4 (.out(button_4_out));
  DotMatrix dotmatrix_1 (.col0(in_14), .col1(in_15), .col2(in_16), .col3(in_17), .col4(in_18));
  Hex_Digit_Display hex_digit_display_1 (.value(in_8), .dp(in_10));
  _7_Segment_Display u_7_segment_display_1 (
    .g(in_5), .f(in_3), .a(in_2), .b(in_1), .e(in_7), .d(in_9), .c(in_11), .dp(in_12));
endmodule
